// Logisim project Nibadder.circ as structural Verilog: 1 circuit, main circuit main
module main (
  input  cin,
  input  [3:0] inputA,
  input  [3:0] inputB,
  output [3:0] AplusB,
  output Carry
);

  wire and_1_out, and_2_out, and_3_out, and_4_out, and_5_out, and_6_out, and_7_out, and_8_out, and_9_out,
       and_10_out, and_11_out, and_12_out, or_1_out, or_2_out, or_3_out, or_4_out, or_5_out, or_6_out,
       or_7_out, xor_1_out, xor_2_out, xor_3_out, xor_4_out;

  and and_1 (and_1_out, cin, inputB[0]);
  and and_2 (and_2_out, cin, inputA[0]);
  and and_3 (and_3_out, inputA[0], inputB[0]);
  and and_4 (and_4_out, or_5_out, inputB[1]);
  and and_5 (and_5_out, or_5_out, inputA[1]);
  and and_6 (and_6_out, inputA[1], inputB[1]);
  xor xor_1 (xor_1_out, or_6_out, inputA[2]);
  and and_7 (and_7_out, or_6_out, inputB[2]);
  and and_8 (and_8_out, or_6_out, inputA[2]);
  and and_9 (and_9_out, inputA[2], inputB[2]);
  xor xor_2 (xor_2_out, or_7_out, inputA[3]);
  and and_10 (and_10_out, or_7_out, inputB[3]);
  and and_11 (and_11_out, or_7_out, inputA[3]);
  and and_12 (and_12_out, inputA[3], inputB[3]);
  xor xor_3 (xor_3_out, cin, inputA[0]);
  xor xor_4 (xor_4_out, or_5_out, inputA[1]);
  xor xor_5 (AplusB[3], xor_2_out, inputB[3]);
  xor xor_6 (AplusB[0], xor_3_out, inputB[0]);
  or or_1 (or_1_out, and_2_out, and_3_out);
  xor xor_7 (AplusB[1], xor_4_out, inputB[1]);
  or or_2 (or_2_out, and_5_out, and_6_out);
  xor xor_8 (AplusB[2], xor_1_out, inputB[2]);
  or or_3 (or_3_out, and_8_out, and_9_out);
  or or_4 (or_4_out, and_11_out, and_12_out);
  or or_5 (or_5_out, and_1_out, or_1_out);
  or or_6 (or_6_out, and_4_out, or_2_out);
  or or_7 (or_7_out, and_7_out, or_3_out);
  or or_8 (Carry, and_10_out, or_4_out);

  // Notes on the sheet:
  //   Jack Patterson
  //   Dylan Faulhaber
  //   I pledge my honor that I have abided by the Stevens Honor System
endmodule
