// Logisim project lab8.circ as structural Verilog: 1 circuit, main circuit main
module main (
  output [7:0] out_1
);

  wire adder_1_cout, clock_1_out;
  wire [7:0] adder_1_out, PC_Register_q;

  Adder adder_1 (.a(PC_Register_q), .b(8'h1), .out(adder_1_out), .cin(adder_1_cout), .cout(adder_1_cout));
  Register PC_Register (.D(adder_1_out), .en(1'b1), .clk(clock_1_out), .Q(PC_Register_q));  // open: clr
  Clock clock_1 (.out(clock_1_out));
  RAM ram_1 (.addr(PC_Register_q), .we(1'b0), .oe(1'b1), .clk(clock_1_out), .dout(out_1));  // open: din

  // Notes on the sheet:
  //   Dylan Faulhaber
  //   Jack Patterson
  //   I pledge my honor that I have abided by the Stevens Honor System
endmodule
