// Logisim project project2 CPU.circ as structural Verilog: 1 circuit, main circuit main
module main (
);

  wire adder_1_cout, and_1_out, and_2_out, and_3_out, and_4_out, buffer_1_out, buffer_2_out, buffer_3_out,
       buffer_4_out, buffer_5_out, buffer_6_out, buffer_7_out, buffer_8_out, buffer_9_out, buffer_10_out,
       buffer_11_out, buffer_12_out, buffer_13_out, buffer_14_out, buffer_15_out, buffer_16_out,
       buffer_17_out, buffer_18_out, buffer_19_out, buffer_20_out, buffer_21_out, buffer_22_out,
       buffer_23_out, buffer_24_out, buffer_25_out, buffer_26_out, buffer_27_out, buffer_28_out,
       buffer_29_out, buffer_30_out, buffer_31_out, buffer_32_out, buffer_33_out, buffer_34_out,
       buffer_35_out, buffer_36_out, buffer_37_out, buffer_38_out, buffer_39_out, buffer_40_out,
       buffer_41_out, buffer_42_out, buffer_43_out, buffer_44_out, buffer_45_out, buffer_46_out,
       buffer_47_out, buffer_48_out, buffer_49_out, buffer_50_out, buffer_51_out, buffer_52_out,
       buffer_53_out, buffer_54_out, buffer_55_out, buffer_56_out, buffer_57_out, buffer_58_out,
       buffer_59_out, buffer_60_out, buffer_61_out, buffer_62_out, buffer_63_out, buffer_64_out,
       buffer_65_out, buffer_66_out, buffer_67_out, buffer_68_out, buffer_69_out, buffer_70_out,
       buffer_71_out, buffer_72_out, buffer_73_out, buffer_74_out, buffer_75_out, buffer_76_out,
       buffer_77_out, buffer_78_out, buffer_79_out, buffer_80_out, buffer_81_out, buffer_82_out,
       buffer_83_out, buffer_84_out, buffer_85_out, clock_1_out, decoder_1_out1, decoder_1_out2,
       decoder_1_out3, decoder_2_out0, decoder_2_out1, decoder_2_out2, decoder_2_out3, decoder_3_out0,
       decoder_3_out1, decoder_3_out2, decoder_3_out3, not_1_out, not_2_out, not_3_out, not_4_out, not_5_out,
       not_6_out, not_7_out, not_8_out, not_9_out, not_10_out, not_11_out, not_12_out, not_13_out,
       not_14_out, not_15_out, not_16_out, not_17_out, not_18_out, not_19_out, not_20_out, not_21_out,
       not_22_out, not_23_out, not_24_out, not_25_out, not_26_out, not_27_out, not_28_out, not_29_out,
       not_30_out, not_31_out, not_32_out, or_1_out, or_2_out, or_3_out, or_4_out;
  wire [7:0] adder_1_out, adder_2_out, Data_Memory_dout, Instruction_Memory_dout, multiplexer_1_out,
       multiplexer_2_out, multiplexer_3_out, multiplexer_4_out, multiplexer_5_out, Program_Counter_q, Reg0_q,
       Reg1_q, Reg2_q, Reg3_q, subtractor_1_out;

  Adder adder_1 (.a(Program_Counter_q), .b(8'h1), .out(adder_1_out), .cin(adder_1_cout), .cout(adder_1_cout));
  Register Program_Counter (.D(adder_1_out), .en(1'b1), .clk(clock_1_out), .Q(Program_Counter_q));  // open: clr
  Clock clock_1 (.out(clock_1_out));
  RAM Instruction_Memory (
    .addr(Program_Counter_q), .we(1'b0), .oe(1'b1), .clk(clock_1_out), .dout(Instruction_Memory_dout));  // open: din
  not not_1 (not_1_out, Instruction_Memory_dout[7]);
  _7_Segment_Display u_7_segment_display_1 (
    .f(not_1_out), .a(not_1_out), .b(1'b1), .e(not_1_out), .d(not_1_out), .c(1'b1));  // open: g, dp
  buf buffer_1 (buffer_1_out, clock_1_out);
  buf buffer_2 (buffer_2_out, buffer_1_out);
  buf buffer_3 (buffer_3_out, buffer_2_out);
  buf buffer_4 (buffer_4_out, buffer_3_out);
  buf buffer_5 (buffer_5_out, buffer_52_out);
  buf buffer_6 (buffer_6_out, buffer_5_out);
  buf buffer_7 (buffer_7_out, buffer_6_out);
  buf buffer_8 (buffer_8_out, buffer_7_out);
  not not_2 (not_2_out, Instruction_Memory_dout[6]);
  not not_3 (not_3_out, Instruction_Memory_dout[5]);
  _7_Segment_Display u_7_segment_display_2 (
    .f(not_2_out), .a(not_2_out), .b(1'b1), .e(not_2_out), .d(not_2_out), .c(1'b1));  // open: g, dp
  _7_Segment_Display u_7_segment_display_3 (
    .f(not_3_out), .a(not_3_out), .b(1'b1), .e(not_3_out), .d(not_3_out), .c(1'b1));  // open: g, dp
  buf buffer_9 (buffer_9_out, buffer_4_out);
  buf buffer_10 (buffer_10_out, buffer_9_out);
  buf buffer_11 (buffer_11_out, buffer_10_out);
  buf buffer_12 (buffer_12_out, buffer_11_out);
  buf buffer_13 (buffer_13_out, buffer_8_out);
  buf buffer_14 (buffer_14_out, buffer_13_out);
  buf buffer_15 (buffer_15_out, buffer_14_out);
  buf buffer_16 (buffer_16_out, buffer_15_out);
  not not_4 (not_4_out, Instruction_Memory_dout[4]);
  not not_5 (not_5_out, Instruction_Memory_dout[3]);
  _7_Segment_Display u_7_segment_display_4 (
    .f(not_4_out), .a(not_4_out), .b(1'b1), .e(not_4_out), .d(not_4_out), .c(1'b1));  // open: g, dp
  _7_Segment_Display u_7_segment_display_5 (
    .f(not_5_out), .a(not_5_out), .b(1'b1), .e(not_5_out), .d(not_5_out), .c(1'b1));  // open: g, dp
  buf buffer_17 (buffer_17_out, buffer_12_out);
  buf buffer_18 (buffer_18_out, buffer_17_out);
  buf buffer_19 (buffer_19_out, buffer_18_out);
  buf buffer_20 (buffer_20_out, buffer_19_out);
  buf buffer_21 (buffer_21_out, buffer_16_out);
  buf buffer_22 (buffer_22_out, buffer_21_out);
  buf buffer_23 (buffer_23_out, buffer_22_out);
  buf buffer_24 (buffer_24_out, buffer_23_out);
  not not_6 (not_6_out, Instruction_Memory_dout[2]);
  not not_7 (not_7_out, Instruction_Memory_dout[1]);
  _7_Segment_Display u_7_segment_display_6 (
    .f(not_6_out), .a(not_6_out), .b(1'b1), .e(not_6_out), .d(not_6_out), .c(1'b1));  // open: g, dp
  _7_Segment_Display u_7_segment_display_7 (
    .f(not_7_out), .a(not_7_out), .b(1'b1), .e(not_7_out), .d(not_7_out), .c(1'b1));  // open: g, dp
  buf buffer_25 (buffer_25_out, buffer_20_out);
  buf buffer_26 (buffer_26_out, buffer_25_out);
  buf buffer_27 (buffer_27_out, buffer_26_out);
  buf buffer_28 (buffer_28_out, buffer_27_out);
  buf buffer_29 (buffer_29_out, buffer_24_out);
  buf buffer_30 (buffer_30_out, buffer_29_out);
  buf buffer_31 (buffer_31_out, buffer_30_out);
  buf buffer_32 (buffer_32_out, buffer_31_out);
  not not_8 (not_8_out, Instruction_Memory_dout[0]);
  _7_Segment_Display u_7_segment_display_8 (
    .f(not_8_out), .a(not_8_out), .b(1'b1), .e(not_8_out), .d(not_8_out), .c(1'b1));  // open: g, dp
  Decoder #(.select(2)) decoder_1 (
    .out1(decoder_1_out1), .out2(decoder_1_out2), .out3(decoder_1_out3), .sel(Instruction_Memory_dout[7:6]));  // open: out0, en
  buf buffer_33 (buffer_33_out, buffer_36_out);
  buf buffer_34 (buffer_34_out, buffer_33_out);
  buf buffer_35 (buffer_35_out, buffer_28_out);
  buf buffer_36 (buffer_36_out, buffer_35_out);
  buf buffer_37 (buffer_37_out, buffer_40_out);
  buf buffer_38 (buffer_38_out, buffer_37_out);
  buf buffer_39 (buffer_39_out, buffer_32_out);
  buf buffer_40 (buffer_40_out, buffer_39_out);
  or or_1 (or_1_out, decoder_1_out1, decoder_1_out2);
  Decoder #(.select(2)) decoder_2 (
    .out0(decoder_2_out0), .out1(decoder_2_out1), .out2(decoder_2_out2), .out3(decoder_2_out3),
    .sel(Instruction_Memory_dout[5:4]));  // open: en
  buf buffer_41 (buffer_41_out, buffer_34_out);
  buf buffer_42 (buffer_42_out, buffer_41_out);
  buf buffer_43 (buffer_43_out, buffer_42_out);
  buf buffer_44 (buffer_44_out, buffer_43_out);
  buf buffer_45 (buffer_45_out, buffer_38_out);
  buf buffer_46 (buffer_46_out, buffer_45_out);
  buf buffer_47 (buffer_47_out, buffer_46_out);
  buf buffer_48 (buffer_48_out, buffer_47_out);
  or or_2 (or_2_out, or_1_out, decoder_1_out3);
  buf buffer_49 (buffer_49_out, buffer_44_out);
  buf buffer_50 (buffer_50_out, buffer_49_out);
  buf buffer_51 (buffer_51_out, buffer_50_out);
  buf buffer_52 (buffer_52_out, buffer_51_out);
  buf buffer_53 (buffer_53_out, buffer_48_out);
  buf buffer_54 (buffer_54_out, buffer_53_out);
  buf buffer_55 (buffer_55_out, buffer_54_out);
  buf buffer_56 (buffer_56_out, buffer_55_out);
  not not_9 (not_9_out, multiplexer_2_out[7]);
  not not_10 (not_10_out, multiplexer_2_out[6]);
  _7_Segment_Display u_7_segment_display_9 (
    .f(not_9_out), .a(not_9_out), .b(1'b1), .e(not_9_out), .d(not_9_out), .c(1'b1));  // open: g, dp
  _7_Segment_Display u_7_segment_display_10 (
    .f(not_10_out), .a(not_10_out), .b(1'b1), .e(not_10_out), .d(not_10_out), .c(1'b1));  // open: g, dp
  not not_11 (not_11_out, multiplexer_2_out[5]);
  not not_12 (not_12_out, multiplexer_2_out[4]);
  _7_Segment_Display u_7_segment_display_11 (
    .f(not_11_out), .a(not_11_out), .b(1'b1), .e(not_11_out), .d(not_11_out), .c(1'b1));  // open: g, dp
  _7_Segment_Display u_7_segment_display_12 (
    .f(not_12_out), .a(not_12_out), .b(1'b1), .e(not_12_out), .d(not_12_out), .c(1'b1));  // open: g, dp
  and and_1 (and_1_out, or_2_out, decoder_2_out0);
  and and_2 (and_2_out, or_2_out, decoder_2_out1);
  and and_3 (and_3_out, or_2_out, decoder_2_out2);
  and and_4 (and_4_out, or_2_out, decoder_2_out3);
  not not_13 (not_13_out, multiplexer_2_out[3]);
  not not_14 (not_14_out, multiplexer_2_out[2]);
  _7_Segment_Display u_7_segment_display_13 (
    .f(not_13_out), .a(not_13_out), .b(1'b1), .e(not_13_out), .d(not_13_out), .c(1'b1));  // open: g, dp
  _7_Segment_Display u_7_segment_display_14 (
    .f(not_14_out), .a(not_14_out), .b(1'b1), .e(not_14_out), .d(not_14_out), .c(1'b1));  // open: g, dp
  Register Reg0 (.D(multiplexer_5_out), .en(and_1_out), .clk(buffer_56_out), .Q(Reg0_q));  // open: clr
  Register Reg1 (.D(multiplexer_5_out), .en(and_2_out), .clk(buffer_56_out), .Q(Reg1_q));  // open: clr
  Register Reg2 (.D(multiplexer_5_out), .en(and_3_out), .clk(buffer_56_out), .Q(Reg2_q));  // open: clr
  Register Reg3 (.D(multiplexer_5_out), .en(and_4_out), .clk(buffer_56_out), .Q(Reg3_q));  // open: clr
  buf buffer_57 (buffer_57_out, clock_1_out);
  buf buffer_58 (buffer_58_out, buffer_57_out);
  buf buffer_59 (buffer_59_out, buffer_58_out);
  not not_15 (not_15_out, multiplexer_2_out[1]);
  not not_16 (not_16_out, multiplexer_2_out[0]);
  _7_Segment_Display u_7_segment_display_15 (
    .f(not_15_out), .a(not_15_out), .b(1'b1), .e(not_15_out), .d(not_15_out), .c(1'b1));  // open: g, dp
  _7_Segment_Display u_7_segment_display_16 (
    .f(not_16_out), .a(not_16_out), .b(1'b1), .e(not_16_out), .d(not_16_out), .c(1'b1));  // open: g, dp
  buf buffer_60 (buffer_60_out, buffer_59_out);
  buf buffer_61 (buffer_61_out, buffer_60_out);
  buf buffer_62 (buffer_62_out, buffer_61_out);
  buf buffer_63 (buffer_63_out, buffer_62_out);
  buf buffer_64 (buffer_64_out, buffer_63_out);
  buf buffer_65 (buffer_65_out, buffer_64_out);
  buf buffer_66 (buffer_66_out, buffer_65_out);
  buf buffer_67 (buffer_67_out, buffer_66_out);
  Multiplexer #(.select(2), .width(8)) multiplexer_1 (
    .in0(Reg0_q), .in1(Reg1_q), .in2(Reg2_q), .in3(Reg3_q), .out(multiplexer_1_out),
    .sel(Instruction_Memory_dout[5:4]));
  Multiplexer #(.select(2), .width(8)) multiplexer_2 (
    .in0(Reg0_q), .in1(Reg1_q), .in2(Reg2_q), .in3(Reg3_q), .out(multiplexer_2_out),
    .sel(Instruction_Memory_dout[3:2]));
  Multiplexer #(.select(2), .width(8)) multiplexer_3 (
    .in0(Reg0_q), .in1(Reg1_q), .in2(Reg2_q), .in3(Reg3_q), .out(multiplexer_3_out),
    .sel(Instruction_Memory_dout[1:0]));
  buf buffer_68 (buffer_68_out, buffer_67_out);
  buf buffer_69 (buffer_69_out, buffer_68_out);
  buf buffer_70 (buffer_70_out, buffer_69_out);
  buf buffer_71 (buffer_71_out, buffer_70_out);
  not not_17 (not_17_out, multiplexer_3_out[7]);
  not not_18 (not_18_out, multiplexer_3_out[6]);
  _7_Segment_Display u_7_segment_display_17 (
    .f(not_17_out), .a(not_17_out), .b(1'b1), .e(not_17_out), .d(not_17_out), .c(1'b1));  // open: g, dp
  _7_Segment_Display u_7_segment_display_18 (
    .f(not_18_out), .a(not_18_out), .b(1'b1), .e(not_18_out), .d(not_18_out), .c(1'b1));  // open: g, dp
  buf buffer_72 (buffer_72_out, buffer_71_out);
  buf buffer_73 (buffer_73_out, buffer_72_out);
  buf buffer_74 (buffer_74_out, buffer_73_out);
  buf buffer_75 (buffer_75_out, buffer_74_out);
  not not_19 (not_19_out, multiplexer_3_out[5]);
  not not_20 (not_20_out, multiplexer_3_out[4]);
  _7_Segment_Display u_7_segment_display_19 (
    .f(not_19_out), .a(not_19_out), .b(1'b1), .e(not_19_out), .d(not_19_out), .c(1'b1));  // open: g, dp
  _7_Segment_Display u_7_segment_display_20 (
    .f(not_20_out), .a(not_20_out), .b(1'b1), .e(not_20_out), .d(not_20_out), .c(1'b1));  // open: g, dp
  Adder adder_2 (.a(multiplexer_2_out), .b(multiplexer_3_out), .out(adder_2_out));  // open: cin, cout
  Subtractor subtractor_1 (.a(multiplexer_2_out), .b(multiplexer_3_out), .out(subtractor_1_out));  // open: bin, bout
  buf buffer_76 (buffer_76_out, buffer_75_out);
  buf buffer_77 (buffer_77_out, buffer_76_out);
  buf buffer_78 (buffer_78_out, buffer_77_out);
  buf buffer_79 (buffer_79_out, buffer_78_out);
  not not_21 (not_21_out, multiplexer_3_out[3]);
  not not_22 (not_22_out, multiplexer_3_out[2]);
  _7_Segment_Display u_7_segment_display_21 (
    .f(not_21_out), .a(not_21_out), .b(1'b1), .e(not_21_out), .d(not_21_out), .c(1'b1));  // open: g, dp
  _7_Segment_Display u_7_segment_display_22 (
    .f(not_22_out), .a(not_22_out), .b(1'b1), .e(not_22_out), .d(not_22_out), .c(1'b1));  // open: g, dp
  Multiplexer #(.select(2), .width(8)) multiplexer_4 (
    .in0(adder_2_out), .in1(adder_2_out), .in2(adder_2_out), .in3(subtractor_1_out), .out(multiplexer_4_out),
    .sel(Instruction_Memory_dout[7:6]));
  buf buffer_80 (buffer_80_out, buffer_79_out);
  buf buffer_81 (buffer_81_out, buffer_80_out);
  buf buffer_82 (buffer_82_out, buffer_81_out);
  buf buffer_83 (buffer_83_out, buffer_82_out);
  not not_23 (not_23_out, multiplexer_3_out[1]);
  not not_24 (not_24_out, multiplexer_3_out[0]);
  _7_Segment_Display u_7_segment_display_23 (
    .f(not_23_out), .a(not_23_out), .b(1'b1), .e(not_23_out), .d(not_23_out), .c(1'b1));  // open: g, dp
  _7_Segment_Display u_7_segment_display_24 (
    .f(not_24_out), .a(not_24_out), .b(1'b1), .e(not_24_out), .d(not_24_out), .c(1'b1));  // open: g, dp
  Decoder #(.select(2)) decoder_3 (
    .out0(decoder_3_out0), .out1(decoder_3_out1), .out2(decoder_3_out2), .out3(decoder_3_out3),
    .sel(Instruction_Memory_dout[7:6]));  // open: en
  buf buffer_84 (buffer_84_out, buffer_83_out);
  buf buffer_85 (buffer_85_out, buffer_84_out);
  Multiplexer #(.select(2), .width(8)) multiplexer_5 (
    .in0(Data_Memory_dout), .in1(Data_Memory_dout), .in2(multiplexer_4_out), .in3(multiplexer_4_out),
    .out(multiplexer_5_out), .sel(Instruction_Memory_dout[7:6]));
  not not_25 (not_25_out, multiplexer_5_out[7]);
  _7_Segment_Display u_7_segment_display_25 (
    .f(not_25_out), .a(not_25_out), .b(1'b1), .e(not_25_out), .d(not_25_out), .c(1'b1));  // open: g, dp
  or or_3 (or_3_out, decoder_3_out2, decoder_3_out1);
  or or_4 (or_4_out, decoder_3_out3, or_3_out);
  RAM Data_Memory (
    .addr(multiplexer_4_out), .we(decoder_3_out0), .oe(or_4_out), .clk(buffer_85_out),
    .din(multiplexer_1_out), .dout(Data_Memory_dout));
  not not_26 (not_26_out, multiplexer_5_out[6]);
  not not_27 (not_27_out, multiplexer_5_out[5]);
  _7_Segment_Display u_7_segment_display_26 (
    .f(not_26_out), .a(not_26_out), .b(1'b1), .e(not_26_out), .d(not_26_out), .c(1'b1));  // open: g, dp
  _7_Segment_Display u_7_segment_display_27 (
    .f(not_27_out), .a(not_27_out), .b(1'b1), .e(not_27_out), .d(not_27_out), .c(1'b1));  // open: g, dp
  not not_28 (not_28_out, multiplexer_5_out[4]);
  not not_29 (not_29_out, multiplexer_5_out[3]);
  _7_Segment_Display u_7_segment_display_28 (
    .f(not_28_out), .a(not_28_out), .b(1'b1), .e(not_28_out), .d(not_28_out), .c(1'b1));  // open: g, dp
  _7_Segment_Display u_7_segment_display_29 (
    .f(not_29_out), .a(not_29_out), .b(1'b1), .e(not_29_out), .d(not_29_out), .c(1'b1));  // open: g, dp
  not not_30 (not_30_out, multiplexer_5_out[2]);
  not not_31 (not_31_out, multiplexer_5_out[1]);
  _7_Segment_Display u_7_segment_display_30 (
    .f(not_30_out), .a(not_30_out), .b(1'b1), .e(not_30_out), .d(not_30_out), .c(1'b1));  // open: g, dp
  _7_Segment_Display u_7_segment_display_31 (
    .f(not_31_out), .a(not_31_out), .b(1'b1), .e(not_31_out), .d(not_31_out), .c(1'b1));  // open: g, dp
  not not_32 (not_32_out, multiplexer_5_out[0]);
  _7_Segment_Display u_7_segment_display_32 (
    .f(not_32_out), .a(not_32_out), .b(1'b1), .e(not_32_out), .d(not_32_out), .c(1'b1));  // open: g, dp

  // Notes on the sheet:
  //   Dylan Faulhaber
  //   Jack Patterson
  //   I pledge my honor that I have abided by the Stevens Honor System
  //   CPU Name: I took CS 382 and all I got was this sucky CPU
  //   Machine Code for current Instruction
  //   opCode
  //   targetReg/Reg3
  //   Reg1
  //   Reg2
  //   Data being read from Rn
  //   Reg1 Data
  //   Reg2 Data
  //   Reg3 data for STO
  //   Data being read from Rm
  //   Result of Multiplexor
endmodule
